// Logisim project mrk133_proj2.circ as structural Verilog: 6 circuits, main circuit main
module main (
);

  wire ALUbsrc, and_1_out, beq, bge, blt, bne, branch, button_1_out, CLK, clock_1_out, comparator_1_gt,
       dispWE, HALT, jr, jump, MemWE, multiplexer_1_out, regwe;
  wire [1:0] bSelectSrc;
  wire [2:0] aluop, rd, RegDataSrc, rs, rt;
  wire [3:0] display_unit_1_digit0, display_unit_1_digit1, display_unit_1_digit2, display_unit_1_digit3;
  wire [7:0] PC_FSM_pc_out;
  wire [15:0] alu, DataMemOut, imm, imm____8, multiplexer_2_out, multiplexer_3_out, multiplexer_4_out,
       PC___1, REG_rs, REG_rt;
  wire [21:0] rom_1_data;

  Clock clock_1 (.out(clock_1_out));
  Button button_1 (.out(button_1_out));
  or or_1 (CLK, clock_1_out, button_1_out);
  Multiplexer #(.select(2)) multiplexer_1 (
    .in0(blt), .in1(bge), .in2(beq), .in3(bne), .out(multiplexer_1_out), .sel(bSelectSrc));  // open: en
  Comparator #(.width(16)) comparator_1 (.a(alu), .b({16{1'b0}}), .gt(comparator_1_gt), .eq(beq), .lt(blt));
  Multiplexer #(.select(3), .width(16)) multiplexer_2 (
    .in0(alu), .in1(imm), .in2(imm____8), .in3(REG_rs), .in4(DataMemOut), .in5(PC___1),
    .out(multiplexer_2_out), .sel(RegDataSrc));  // open: in6, in7, en
  Multiplexer #(.width(16)) multiplexer_3 (
    .in0(REG_rt), .in1(imm), .out(multiplexer_3_out), .sel(ALUbsrc));  // open: en
  and and_1 (and_1_out, multiplexer_1_out, branch);
  // OR_Gate or_2: pin names not known; wires that end beside it: comparator_1_gt, beq, bge
  // NOT_Gate not_1: pin names not known; wires that end beside it: beq, bne
  Hex_Digit_Display hex_digit_display_1 (.value(display_unit_1_digit0));  // open: dp
  Display_Unit display_unit_1 (
    .Data(REG_rs), .Digit0(display_unit_1_digit0), .Digit1(display_unit_1_digit1),
    .Digit2(display_unit_1_digit2), .Digit3(display_unit_1_digit3), .WriteEn(dispWE), .Clock(CLK));
  Register_File register_file_1 (
    .REG_rd(multiplexer_2_out), .Reg_WE(regwe), .rd(rd), .rs(rs), .rt(rt), .clock(CLK), .REG_rs(REG_rs),
    .REG_rt(REG_rt));
  ALU alu_1 (.A(REG_rs), .B(multiplexer_3_out), .Operation(aluop), .Result(alu));
  Multiplexer #(.width(16)) multiplexer_4 (.in0(imm), .in1(REG_rs), .out(multiplexer_4_out), .sel(jr));  // open: en
  Hex_Digit_Display hex_digit_display_2 (.value(display_unit_1_digit1));  // open: dp
  Hex_Digit_Display hex_digit_display_3 (.value(display_unit_1_digit2));  // open: dp
  PC_FSM PC_FSM (
    .Clock(CLK), .Offset(imm), .Target(multiplexer_4_out), .Jump(jump), .Branch(and_1_out), .Halt(HALT),
    .PC_Out(PC_FSM_pc_out), .PC_1_Out(PC___1));
  Hex_Digit_Display hex_digit_display_4 (.value(display_unit_1_digit3));  // open: dp
  LED u_HALT (.in(HALT));
  // Probe on PC_FSM_pc_out
  The_Control the_control_1 (
    .Instruction(rom_1_data), .rt(rt), .rs(rs), .rd(rd), .halt(HALT), .Display_WE(dispWE), .Reg_WE(regwe),
    .imm____8(imm____8), .RegDataSrc(RegDataSrc), .imm(imm), .ALUbsrc(ALUbsrc), .MemWE(MemWE), .ALUOp(aluop),
    .jump(jump), .branch(branch), .jr(jr), .bSelect(bSelectSrc));
  ROM #(.dataWidth(22)) rom_1 (.addr(PC_FSM_pc_out), .data(rom_1_data));  // open: sel
  RAM #(.addrWidth(16), .dataWidth(16), .bus("separate")) ram_1 (
    .addr(alu), .din(REG_rt), .data(DataMemOut), .str(MemWE), .clk(CLK));  // open: sel, ld, clr

  // Notes on the sheet:
  //   branch comparator
  //   InstMem
  //   contents of rom_1 (hex, n*v repeats v):
  //   40440 20008 40640 40680 320e0a 1e00c8 1000da 320a18 31fc18 1e0490 2c0800 20008 1e0448 2c0600
  //   DataMem
endmodule

// Display
module Display_Unit (
  input  WriteEn,
  input  Clock,
  input  [15:0] Data,
  output [3:0] Digit0,
  output [3:0] Digit1,
  output [3:0] Digit2,
  output [3:0] Digit3
);

  Register #(.width(16)) register_1 (
    .D(Data), .en(WriteEn), .Q({Digit0, Digit1, Digit2, Digit3}), .clk(Clock));  // open: clr
endmodule

module ALU (
  input  [15:0] A,
  input  [15:0] B,
  input  [2:0] Operation,
  output [15:0] Result
);

  wire [3:0] bit_extender_1_out, bit_extender_2_out;
  wire [15:0] A_____B_3_0, A____B_3_0, A___B, A___B_t, A___B_t_t, A___B_t_t_t, A___B_t_t_t_t, nB;

  Adder #(.width(16)) adder_1 (.a(A), .b(B), .out(A___B_t));  // open: cin, cout
  assign A___B_t_t_t = A ^ B;  // XOR_Gate xor_1, 16 bits wide
  Multiplexer #(.select(3), .width(16)) multiplexer_1 (
    .in0(A___B_t), .in1(A___B_t_t), .in2(A___B), .in3(A___B_t_t_t_t), .in4(A___B_t_t_t), .in5(nB),
    .in6(A____B_3_0), .in7(A_____B_3_0), .out(Result), .sel(Operation));  // open: en
  assign nB = ~B;  // NOT_Gate not_1, 16 bits wide
  Subtractor #(.width(16)) subtractor_1 (.a(A), .b(B), .out(A___B_t_t));  // open: bin, bout
  Bit_Extender #(.in_width(16), .out_width(4)) bit_extender_1 (.in(B), .out(bit_extender_1_out));
  assign A___B = A & B;  // AND_Gate and_1, 16 bits wide
  Shifter #(.width(16)) shifter_1 (.in(A), .\dist (bit_extender_1_out), .out(A____B_3_0));
  assign A___B_t_t_t_t = A | B;  // OR_Gate or_1, 16 bits wide
  Bit_Extender #(.in_width(16), .out_width(4)) bit_extender_2 (.in(B), .out(bit_extender_2_out));
  Shifter #(.width(16), .shift("lr")) shifter_2 (.in(A), .\dist (bit_extender_2_out), .out(A_____B_3_0));

  // Notes on the sheet:
  //   A + B
  //   A ^ B
  //   A - B
  //   ~B
  //   A & B
  //   A << B[3:0]
  //   A | B
  //   A >>> B[3:0]
endmodule

module Register_File (
  input  [15:0] REG_rd,
  input  Reg_WE,
  input  [2:0] rd,
  input  [2:0] rs,
  input  [2:0] rt,
  input  clock,
  output [15:0] REG_rs,
  output [15:0] REG_rt
);

  wire demultiplexer_1_out0, demultiplexer_1_out1, demultiplexer_1_out2, demultiplexer_1_out3,
       demultiplexer_1_out4, demultiplexer_1_out5, demultiplexer_1_out6, demultiplexer_1_out7;
  wire [15:0] _1_q, _2_q, _3_q, _4_q, _5_q, _6_q, _7_q;

  Demultiplexer #(.select(3)) demultiplexer_1 (
    .out0(demultiplexer_1_out0), .out1(demultiplexer_1_out1), .out2(demultiplexer_1_out2),
    .out3(demultiplexer_1_out3), .out4(demultiplexer_1_out4), .out5(demultiplexer_1_out5),
    .out6(demultiplexer_1_out6), .out7(demultiplexer_1_out7), .in(Reg_WE), .sel(rd));  // open: en
  Register #(.width(16)) _1 (.D(REG_rd), .en(demultiplexer_1_out1), .Q(_1_q), .clk(clock));  // open: clr
  Register #(.width(16)) _2 (.D(REG_rd), .en(demultiplexer_1_out2), .Q(_2_q), .clk(clock));  // open: clr
  Register #(.width(16)) _3 (.D(REG_rd), .en(demultiplexer_1_out3), .Q(_3_q), .clk(clock));  // open: clr
  Register #(.width(16)) _4 (.D(REG_rd), .en(demultiplexer_1_out4), .Q(_4_q), .clk(clock));  // open: clr
  Register #(.width(16)) _5 (.D(REG_rd), .en(demultiplexer_1_out5), .Q(_5_q), .clk(clock));  // open: clr
  Register #(.width(16)) _6 (.D(REG_rd), .en(demultiplexer_1_out6), .Q(_6_q), .clk(clock));  // open: clr
  Register #(.width(16)) _7 (.D(REG_rd), .en(demultiplexer_1_out7), .Q(_7_q), .clk(clock));  // open: clr
  Multiplexer #(.select(3), .width(16)) multiplexer_1 (
    .in0({16{1'b0}}), .in1(_1_q), .in2(_2_q), .in3(_3_q), .in4(_4_q), .in5(_5_q), .in6(_6_q), .in7(_7_q),
    .out(REG_rs), .sel(rs));  // open: en
  Multiplexer #(.select(3), .width(16)) multiplexer_2 (
    .in0({16{1'b0}}), .in1(_1_q), .in2(_2_q), .in3(_3_q), .in4(_4_q), .in5(_5_q), .in6(_6_q), .in7(_7_q),
    .out(REG_rt), .sel(rt));  // open: en
  // Probe on REG_rs
  // Probe on REG_rt

  // Other names for the same wires on the sheet: CLK = clock
endmodule

module PC_FSM (
  input  Clock,
  input  [15:0] Offset,
  input  [15:0] Target,
  input  Jump,
  input  Branch,
  input  Halt,
  output [7:0] PC_Out,
  output [15:0] PC_1_Out
);

  wire Halt_t;
  wire [7:0] adder_1_out, multiplexer_1_out, multiplexer_2_out, Offset_7_0, Target_7_0;

  not not_1 (Halt_t, Halt);
  Bit_Extender #(.in_width(16), .out_width(8)) bit_extender_1 (.in(Target), .out(Target_7_0));
  Bit_Extender #(.in_width(16), .out_width(8)) bit_extender_2 (.in(Offset), .out(Offset_7_0));
  Multiplexer #(.width(8)) multiplexer_1 (
    .in0(8'h1), .in1(Offset_7_0), .out(multiplexer_1_out), .sel(Branch));  // open: en
  Adder adder_1 (.a(PC_Out), .b(multiplexer_1_out), .out(adder_1_out));  // open: cin, cout
  Register PC (.D(multiplexer_2_out), .en(Halt_t), .Q(PC_Out), .clk(Clock));  // open: clr
  Multiplexer #(.width(8)) multiplexer_2 (
    .in0(adder_1_out), .in1(Target_7_0), .out(multiplexer_2_out), .sel(Jump));  // open: en
  assign PC_1_Out = {{8{1'b0}}, adder_1_out};  // Bit_Extender bit_extender_3

  // Other names for the same wires on the sheet: CLK = Clock

  // Notes on the sheet:
  //   Target [7:0]
  //   Offset [7:0]
endmodule

// Control
module The_Control (
  input  [21:0] Instruction,
  output [2:0] rt,
  output [2:0] rs,
  output [2:0] rd,
  output [15:0] imm,
  output Reg_WE,
  output ALUbsrc,
  output halt,
  output Display_WE,
  output MemWE,
  output [15:0] imm____8,
  output [2:0] RegDataSrc,
  output [2:0] ALUOp,
  output jump,
  output branch,
  output [1:0] bSelect,
  output jr
);

  wire add, adi, \and , ani, beq, bge, blt, bne, decoder_1_p31, decoder_1_p32, decoder_1_p33, j, jal, ld, li,
       lui, mov, \not , \or , or_1_out, or_6_out, or_7_out, or_8_p3, or_9_out, or_10_out, or_11_out,
       or_12_out, ori, sbi, shl, shr, sli, sri, sub, undriven, \xor , xri;
  wire [15:0] bit_extender_1_out, bit_extender_2_out;

  // Decoder #(.select(5)) decoder_1: pin names not known; wires that end beside it: Instruction[21:17], halt, Display_WE, li, lui, mov, ld, MemWE, add, sub, \and , \or , \xor , \not , shl, shr, adi, sbi, ani, ori, xri, sli, sri, j, blt, bge, beq, bne, jal, jr, decoder_1_p31, decoder_1_p32, decoder_1_p33
  or or_1 (or_1_out, MemWE, ld);
  or or_2 (jump, j, jr, jal);
  or or_3 (branch, bge, bne, blt, beq);
  Priority_Encoder #(.select(2)) priority_encoder_1 (
    .in0(1'b1), .in1(bge), .in2(beq), .in3(bne), .out(bSelect));  // open: gs, en_out, en_in
  Shifter #(.width(16)) shifter_1 (.in(imm), .\dist (4'b1000), .out(imm____8));
  Priority_Encoder priority_encoder_2 (
    .in0(1'b1), .in1(li), .in2(lui), .in3(mov), .in4(or_1_out), .in5(jal), .out(RegDataSrc));  // open: in6, in7, en_in, gs, en_out
  or or_4 (Reg_WE, lui, li, ld, mov, add, sub, \and , \or , \xor , \not , shr, shl, sbi, adi, ori, ani, sli, xri, jal, sri);
  assign bit_extender_1_out = {{8{Instruction[16]}}, Instruction[16:9]};  // Bit_Extender bit_extender_1
  assign bit_extender_2_out = {{8{1'b0}}, Instruction[16:9]};  // Bit_Extender bit_extender_2
  or or_5 (ALUbsrc, sbi, ani, ori, MemWE, adi, ld, xri, sli, sri);
  or or_6 (or_6_out, beq, blt, sub, sbi, bge, bne);
  or or_7 (or_7_out, \and , ani);
  // OR_Gate or_8: pin names not known; wires that end beside it: \or , ori, or_8_p3
  or or_9 (or_9_out, \xor , xri);
  or or_10 (or_10_out, shl, sli, undriven);
  or or_11 (or_11_out, undriven, shr, sri);
  Multiplexer #(.width(16)) multiplexer_1 (
    .in0(bit_extender_1_out), .in1(bit_extender_2_out), .out(imm), .sel(or_12_out));  // open: en
  or or_12 (or_12_out, ani, xri, li, ori);
  Priority_Encoder priority_encoder_3 (
    .in0(1'b1), .in1(or_6_out), .in2(or_7_out), .in3(or_8_p3), .in4(or_9_out), .in5(\not ), .in6(or_10_out),
    .in7(or_11_out), .out(ALUOp));  // open: en_in, gs, en_out

  assign rd = Instruction[8:6];
  assign rs = Instruction[5:3];
  assign rt = Instruction[2:0];

  // Other names for the same wires on the sheet: hlt = halt; imm____8_t[15:0] = imm; imm_t[7:0] = Instruction[16:9];
  //   opcode[4:0] = Instruction[21:17]; put = Display_WE; st = MemWE

  // Notes on the sheet:
  //   Instruction Signals
endmodule
